// Digital circuit ALU Register File Connection.dig as structural Verilog
module ALU_Register_File_Connection (
  input  [2:0] SP,
  input  clk,
  input  WR,
  input  WE,
  input  RR1,
  input  RR2,
  output Z
);

  wire _4bit_alu_dlogic_1_p2, _4bit_alu_dlogic_1_p3, _4bit_alu_dlogic_1_p4;

  // _4bit_ALU_dlogic _4bit_alu_dlogic_1: pin names not known; wires that end beside it: SP, _4bit_alu_dlogic_1_p2, _4bit_alu_dlogic_1_p3, _4bit_alu_dlogic_1_p4, Z
  // RegisterFile registerfile_1: pin names not known; wires that end beside it: RR2, RR1, WR, _4bit_alu_dlogic_1_p4, WE, clk, _4bit_alu_dlogic_1_p3, _4bit_alu_dlogic_1_p2
endmodule
