// Digital circuit F_Control_Unit.dig as structural Verilog
module F_Control_Unit (
  input  [3:0] IR,
  input  Z,
  input  CK,
  input  RE,
  output [2:0] ALU_SP,
  output [1:0] RR1,
  output [1:0] RR2,
  output [1:0] WR,
  output [1:0] WE,
  output IL,
  output PC,
  output IF
);

  F_State_Machine f_state_machine_1 (.I(1'b1), .CK(CK));  // open: Q1, Q2
  // F_opcode_Decoder f_opcode_decoder_1: pin names not known; wires that end beside it: IR, Z, CK, RR1, RR2, RR2, IL, WR, ALU_SP, PC, IF
  // Pins of 1 and 2 bits meet at RR2

  assign WE = RR2;

  // Notes on the sheet:
  //   Inputs for Control Unit
  //   State Machine
  //   Decoder
  //   CU outputs
endmodule
