// Digital circuit F_State_Machine.dig as structural Verilog
module F_State_Machine (
  input  I,
  input  CK,
  output Q1,
  output Q2
);

  wire and_1_out, and_2_out, and_3_out, and_4_out, and_5_out, not_1_out, not_2_out, not_3_out, not_4_out,
       or_1_out, or_2_out;

  not not_1 (not_1_out, I);
  not not_2 (not_2_out, I);
  not not_3 (not_3_out, Q1);
  not not_4 (not_4_out, Q2);
  and and_1 (and_1_out, Q1, not_1_out);
  and and_2 (and_2_out, Q2, not_2_out);
  and and_3 (and_3_out, not_3_out, not_4_out);
  and and_4 (and_4_out, Q2, I);
  and and_5 (and_5_out, and_3_out, I);
  or or_1 (or_1_out, and_1_out, and_4_out);
  or or_2 (or_2_out, and_2_out, and_5_out);
  D_FF MSB (.D(or_1_out), .C(CK), .Q(Q1));  // open: nQ
  D_FF LSB (.D(or_2_out), .C(CK), .Q(Q2));  // open: nQ

  // Notes on the sheet:
  //   DMSB Logic
  //   DLSB Logic
endmodule
