// Digital circuit F_opcode_Decoder.dig as structural Verilog
module F_opcode_Decoder (
  input  A,
  input  B,
  input  C,
  input  D,
  output RR1,
  output RR2,
  output WE,
  output ADD_A_B,
  output IL,
  output WR,
  output SUB_A_B,
  output OR_A_B,
  output AND_A_B,
  output XOR_A_B,
  output SLT_A_B
);

  wire and_1_out, and_2_out, and_3_out, and_4_out, not_1_out, not_2_out, not_3_out, not_4_out, not_5_out,
       not_6_out, not_7_out, not_8_out, not_9_out, not_10_out, not_11_out, not_12_out, not_13_out,
       not_14_out, not_15_out, not_16_out;

  not not_1 (not_1_out, D);
  not not_2 (not_2_out, B);
  not not_3 (not_3_out, C);
  not not_4 (not_4_out, B);
  not not_5 (not_5_out, C);
  not not_6 (not_6_out, B);
  not not_7 (not_7_out, C);
  not not_8 (not_8_out, A);
  not not_9 (not_9_out, A);
  not not_10 (not_10_out, D);
  not not_11 (not_11_out, D);
  not not_12 (not_12_out, B);
  not not_13 (not_13_out, A);
  not not_14 (not_14_out, B);
  not not_15 (not_15_out, C);
  not not_16 (not_16_out, D);
  and and_1 (and_1_out, not_12_out, not_13_out, C);
  and and_2 (and_2_out, not_14_out, not_15_out, not_16_out);
  and and_3 (and_3_out, not_8_out, D);
  and and_4 (and_4_out, not_9_out, C);
  and and_5 (ADD_A_B, A, not_4_out, not_5_out, D);
  and and_6 (SUB_A_B, A, not_2_out, C, not_10_out);
  and and_7 (AND_A_B, A, not_6_out, C, D);
  and and_8 (OR_A_B, A, B, not_3_out, not_1_out);
  and and_9 (XOR_A_B, A, B, not_7_out, D);
  and and_10 (SLT_A_B, A, B, C, not_11_out);
  or or_1 (WR, and_1_out, and_2_out);
  or or_2 (WE, C, D, A);
  or or_3 (IL, and_3_out, and_4_out);
  not not_17 (RR1, A);

  assign RR2 = 1'b1;

  // Notes on the sheet:
  //   Opcode
  //   OR Logic
  //   ADD Logic
  //   SUB Logic
  //   AND Logic
  //   XOR Logic
  //   IL Logic
  //   SLT Logic
  //   WR Logic
  //   WE Logic
  //   Instructions
endmodule
